// Logisim project LC-2200-16.circ as structural Verilog
module _1_bit_adder (
  input  in_1,
  input  in_2,
  input  in_3,
  output out_4,
  output out_5
);

  wire and_1_out, and_2_out, xor_1_out;

  and and_1 (and_1_out, in_1, in_2);
  xor xor_1 (xor_1_out, in_1, in_2);
  and and_2 (and_2_out, xor_1_out, in_3);
  xor xor_2 (out_4, xor_1_out, in_3);
  or or_1 (out_5, and_2_out, and_1_out);

  // Other names for the same wires on the sheet: A = in_1; B = in_2; C_IN = in_3; C_OUT = out_5; S = out_4
endmodule

module _16_bit_adder (
  input  [15:0] in_1,
  input  [15:0] in_2,
  input  in_3,
  output [15:0] out_4,
  output out_5
);

  wire n1_bit_adder_2_out_5, n1_bit_adder_3_out_5, n1_bit_adder_4_out_5, n1_bit_adder_5_out_5,
       n1_bit_adder_6_out_5, n1_bit_adder_7_out_5, n1_bit_adder_8_out_5, n1_bit_adder_9_out_5,
       n1_bit_adder_10_out_5, n1_bit_adder_11_out_5, n1_bit_adder_12_out_5, n1_bit_adder_13_out_5,
       n1_bit_adder_14_out_5, n1_bit_adder_15_out_5, n1_bit_adder_16_out_5;

  _1_bit_adder u_1_bit_adder_1 (
    .in_1(n1_bit_adder_2_out_5), .in_2(in_2[15]), .in_3(in_1[15]), .out_4(out_4[15]), .out_5(out_5));
  _1_bit_adder u_1_bit_adder_2 (
    .in_1(n1_bit_adder_4_out_5), .in_2(in_2[14]), .in_3(in_1[14]), .out_4(out_4[14]),
    .out_5(n1_bit_adder_2_out_5));
  _1_bit_adder u_1_bit_adder_3 (
    .in_1(n1_bit_adder_5_out_5), .in_2(in_2[12]), .in_3(in_1[12]), .out_4(out_4[12]),
    .out_5(n1_bit_adder_3_out_5));
  _1_bit_adder u_1_bit_adder_4 (
    .in_1(n1_bit_adder_3_out_5), .in_2(in_2[13]), .in_3(in_1[13]), .out_4(out_4[13]),
    .out_5(n1_bit_adder_4_out_5));
  _1_bit_adder u_1_bit_adder_5 (
    .in_1(n1_bit_adder_6_out_5), .in_2(in_2[11]), .in_3(in_1[11]), .out_4(out_4[11]),
    .out_5(n1_bit_adder_5_out_5));
  _1_bit_adder u_1_bit_adder_6 (
    .in_1(n1_bit_adder_7_out_5), .in_2(in_2[10]), .in_3(in_1[10]), .out_4(out_4[10]),
    .out_5(n1_bit_adder_6_out_5));
  _1_bit_adder u_1_bit_adder_7 (
    .in_1(n1_bit_adder_8_out_5), .in_2(in_2[9]), .in_3(in_1[9]), .out_4(out_4[9]),
    .out_5(n1_bit_adder_7_out_5));
  _1_bit_adder u_1_bit_adder_8 (
    .in_1(n1_bit_adder_9_out_5), .in_2(in_2[8]), .in_3(in_1[8]), .out_4(out_4[8]),
    .out_5(n1_bit_adder_8_out_5));
  _1_bit_adder u_1_bit_adder_9 (
    .in_1(n1_bit_adder_10_out_5), .in_2(in_2[7]), .in_3(in_1[7]), .out_4(out_4[7]),
    .out_5(n1_bit_adder_9_out_5));
  _1_bit_adder u_1_bit_adder_10 (
    .in_1(n1_bit_adder_12_out_5), .in_2(in_2[6]), .in_3(in_1[6]), .out_4(out_4[6]),
    .out_5(n1_bit_adder_10_out_5));
  _1_bit_adder u_1_bit_adder_11 (
    .in_1(n1_bit_adder_13_out_5), .in_2(in_2[4]), .in_3(in_1[4]), .out_4(out_4[4]),
    .out_5(n1_bit_adder_11_out_5));
  _1_bit_adder u_1_bit_adder_12 (
    .in_1(n1_bit_adder_11_out_5), .in_2(in_2[5]), .in_3(in_1[5]), .out_4(out_4[5]),
    .out_5(n1_bit_adder_12_out_5));
  _1_bit_adder u_1_bit_adder_13 (
    .in_1(n1_bit_adder_14_out_5), .in_2(in_2[3]), .in_3(in_1[3]), .out_4(out_4[3]),
    .out_5(n1_bit_adder_13_out_5));
  _1_bit_adder u_1_bit_adder_14 (
    .in_1(n1_bit_adder_16_out_5), .in_2(in_2[2]), .in_3(in_1[2]), .out_4(out_4[2]),
    .out_5(n1_bit_adder_14_out_5));
  _1_bit_adder u_1_bit_adder_15 (
    .in_1(in_3), .in_2(in_2[0]), .in_3(in_1[0]), .out_4(out_4[0]), .out_5(n1_bit_adder_15_out_5));
  _1_bit_adder u_1_bit_adder_16 (
    .in_1(n1_bit_adder_15_out_5), .in_2(in_2[1]), .in_3(in_1[1]), .out_4(out_4[1]),
    .out_5(n1_bit_adder_16_out_5));

  // Other names for the same wires on the sheet: A[15:0] = in_1; B[15:0] = in_2; C_IN = in_3; C_OUT = out_5;
  //   S[15:0] = out_4
endmodule

module _16_bit_ALU (
  input  [15:0] in_1,
  input  [15:0] in_2,
  input  [1:0] in_3,
  output [15:0] out_4
);

  wire S0, S1, S2;
  wire [15:0] and_1_out, n16_bit_adder_1_out_4, n16_bit_adder_2_out_4, nand_1_out, not_1_out;

  _16_bit_adder u_16_bit_adder_1 (.in_1(in_1), .in_2(in_2), .in_3(1'b0), .out_4(n16_bit_adder_1_out_4));  // open: out_5
  assign and_1_out = in_1 & not_1_out;  // AND_Gate and_1, 16 bits wide
  assign not_1_out = ~in_2;  // NOT_Gate not_1, 16 bits wide
  _16_bit_adder u_16_bit_adder_2 (
    .in_1(in_1), .in_2(16'h1), .in_3(1'b0), .out_4(n16_bit_adder_2_out_4));  // open: out_5
  assign nand_1_out = ~(in_1 & in_2);  // NAND_Gate nand_1, 16 bits wide
  Multiplexer #(.select(2), .width(16), .disabled(0), .enable("false")) multiplexer_1 (
    .in0(n16_bit_adder_1_out_4), .in1(and_1_out), .in2(n16_bit_adder_2_out_4), .in3(nand_1_out), .out(out_4),
    .sel(in_3));
  Multiplexer #(.select(3), .width(16), .disabled(0), .enable("false")) multiplexer_2 (
    .out(out_4), .sel({S2, S1, S0}));  // open: in0, in1, in2, in3, in4, in5, in6, in7

  // Other names for the same wires on the sheet: A[15:0] = in_1; B[15:0] = in_2; Out[15:0] = out_4; Sel[1:0] = in_3

  // Notes on the sheet:
  //   Add
  //   Sub
  //   Incr
  //   Nand
endmodule
